# Fritzing sketch Montagem (saved by Fritzing 0.9.3b)
breadboards: 1

parts:
  Componente1 = Arduino Uno (Rev3)
  hc-sr1 = hc-sr04

nets:
  N1: Componente1.D11_PWM/MOSI, hc-sr1.Trig
  N2: Componente1.D12/MISO, hc-sr1.Echo
  5V: Componente1.5V, hc-sr1.VCC
  GND: Componente1.GND, hc-sr1.GND
